// Logisim project Lab 3 Given.circ as structural Verilog: 11 circuits, main circuit Main
module Main (
);

  wire ALUSrcA, and_1_out, Branch, CLK, IorD, IRWrite, JAL, jal_t, jr, Jump, MemRead, MemtoReg, MemWrite,
       or_1_out, or_2_out, PCWrite, PCWriteCond, RegDst, RegWrite, Zero;
  wire [1:0] ALUOp, ALUSrcB, PCSource;
  wire [3:0] ALUCtl, multiplexer_7_out;
  wire [4:0] multiplexer_3_out, WrAddr;
  wire [5:0] Func;
  wire [7:0] adder_1_out, multiplexer_1_out, multiplexer_2_out;
  wire [15:6] Instr0_16;
  wire [31:0] A_q, adder_2_out, alu_1_aluresult, ALUout, bit_extender_1_out, MDR, MemData, multiplexer_4_out,
       multiplexer_5_out, multiplexer_6_out, multiplexer_8_out, Offset, PC, PCin, ram_1_data,
       register_file_1_rddata2, RSAddr, WrDataReg, WriteData;
  wire [31:16] IR;

  // Probe on PCin
  Register #(.width(32)) u_PC (.D(PCin), .en(or_1_out), .Q(PC), .clk(CLK));  // open: clr
  or or_1 (or_1_out, PCWrite, and_1_out);
  Clock clock_1 (.out(CLK));
  Multiplexer #(.width(8), .enable("false")) multiplexer_1 (
    .in0(PC[9:2]), .in1(ALUout[7:0]), .out(multiplexer_1_out), .sel(IorD));
  and and_1 (and_1_out, PCWriteCond, Zero);
  // Probe on adder_1_out
  Adder adder_1 (.a(multiplexer_1_out), .b(8'h80), .out(adder_1_out));  // open: cin, cout
  Multiplexer #(.width(8), .enable("false")) multiplexer_2 (
    .in0(multiplexer_1_out), .in1(adder_1_out), .out(multiplexer_2_out), .sel(IorD));
  RAM #(.dataWidth(32), .bus("separate")) ram_1 (
    .addr(multiplexer_2_out), .din(WriteData), .data(ram_1_data), .str(MemWrite), .clk(CLK));  // open: sel, ld, clr
  Register #(.width(32)) u_IR (.D(ram_1_data), .en(IRWrite), .Q({IR, Instr0_16, Func}), .clk(CLK));  // open: clr
  Register #(.width(32)) u_MDR (.D(ram_1_data), .en(IorD), .Q(MDR), .clk(CLK));  // open: clr
  Multiplexer #(.select(2), .width(5), .enable("false")) multiplexer_3 (
    .in0(IR[20:16]), .in1(Instr0_16[15:11]), .in2({5{1'b1}}), .out(multiplexer_3_out), .sel({JAL, RegDst}));  // open: in3
  Multiplexer #(.select(2), .width(32), .enable("false")) multiplexer_4 (
    .in0(ALUout), .in1(MDR), .in2(PC), .out(multiplexer_4_out), .sel({JAL, MemtoReg}));  // open: in3
  Ctl ctl_1 (
    .Op(IR[31:26]), .Func(Func), .Clock(CLK), .PCWrite(PCWrite), .PCWriteCond(PCWriteCond), .IorD(IorD),
    .MemRead(MemRead), .MemWrite(MemWrite), .IRWrite(IRWrite), .MemtoReg(MemtoReg), .PCSource1(PCSource[1]),
    .PCSource0(PCSource[0]), .ALUOp1(ALUOp[1]), .ALUOp0(ALUOp[0]), .ALUSrcB1(ALUSrcB[1]),
    .ALUSrcB0(ALUSrcB[0]), .ALUSrcA(ALUSrcA), .RegWrite(RegWrite), .RegDst(RegDst), .JAL(JAL));
  // Probe on multiplexer_4_out
  or or_2 (or_2_out, RegWrite, JAL);
  // Probe on IR[25:21]
  // Probe on IR[20:16]
  // Probe on multiplexer_3_out
  Register_File register_file_1 (
    .WrAddr(multiplexer_3_out), .WrData(multiplexer_4_out), .WrReg(or_2_out), .RdAddr1(IR[25:21]),
    .RdAddr2(IR[20:16]), .RdData1(RSAddr), .RdData2(register_file_1_rddata2), .Clock(CLK));
  Register #(.width(32)) A (.D(RSAddr), .Q(A_q), .clk(CLK));  // open: en, clr
  Register #(.width(32)) B (.D(register_file_1_rddata2), .Q(WriteData), .clk(CLK));  // open: en, clr
  assign bit_extender_1_out = {{16{Instr0_16[15]}}, {Instr0_16, Func}};  // Bit_Extender bit_extender_1
  // Probe on bit_extender_1_out
  Shifter #(.width(32)) shifter_1 (.in(bit_extender_1_out), .\dist (5'b00010), .out(Offset));
  Multiplexer #(.width(32), .enable("false")) multiplexer_5 (
    .in0(PC), .in1(A_q), .out(multiplexer_5_out), .sel(ALUSrcA));
  ALU alu_1 (
    .ALUCtl(multiplexer_7_out), .A(multiplexer_5_out), .B(multiplexer_6_out), .ALUResult(alu_1_aluresult),
    .Zero(Zero), .Shamt(Instr0_16[10:6]));  // open: Overflow
  Multiplexer #(.select(2), .width(32), .enable("false")) multiplexer_6 (
    .in0(WriteData), .in1(32'h4), .in2(bit_extender_1_out), .in3(Offset), .out(multiplexer_6_out),
    .sel(ALUSrcB));
  // Probe on Func
  Multiplexer #(.width(4), .enable("false")) multiplexer_7 (
    .in0(ALUCtl), .in1(4'b0011), .out(multiplexer_7_out), .sel(IRWrite));
  ALUCtl aluctl_1 (.Op(IR[31:26]), .Func(Func), .ALUOp(ALUOp), .ALUCtl(ALUCtl));  // open: jr
  // Probe on ALUCtl
  Register #(.width(32)) u_ALUout (.D(alu_1_aluresult), .Q(ALUout), .clk(CLK));  // open: en, clr
  // Probe on alu_1_aluresult
  Multiplexer #(.select(2), .width(32), .enable("false")) multiplexer_8 (
    .in0(alu_1_aluresult), .in1(ALUout), .in2({PC[31:28], IR[25:16], Instr0_16, Func, 2'b00}), .in3(RSAddr),
    .out(multiplexer_8_out), .sel(PCSource));
  Adder #(.width(32)) adder_2 (.a(PC), .b(Offset), .out(adder_2_out));  // open: cin, cout
  Multiplexer #(.width(32), .enable("false")) multiplexer_9 (
    .in0(multiplexer_8_out), .in1(adder_2_out), .out(PCin), .sel(Zero));
  // Probe on PC
  // Probe on Branch
  // Probe on Jump
  // Probe on jal_t
  // Probe on jr
  // Probe on RegWrite
  // Probe on WrAddr
  // Probe on WrDataReg
  // Probe on MemWrite
  // Probe on MemData

  // Other names for the same wires on the sheet: Instr0_16[5:0] = Func; IR[15:0] = {Instr0_16, Func};
  //   RDAddr2[4:0] = IR[20:16]; Opcode[5:0] = IR[31:26]
endmodule

module _32_Bit_Adder___Subtractor (
  input  Add_Sub_control,
  input  [31:0] in_2,
  input  [31:0] in_3,
  output [31:0] out_4,
  output carry_out
);

  wire adder_1_cout, subtractor_1_bout;
  wire [31:0] adder_1_out, subtractor_1_out;

  Adder #(.width(32)) adder_1 (.a(in_2), .b(in_3), .out(adder_1_out), .cout(adder_1_cout));  // open: cin
  Subtractor #(.width(32)) subtractor_1 (
    .a(in_2), .b(in_3), .out(subtractor_1_out), .bout(subtractor_1_bout));  // open: bin
  Multiplexer #(.width(32), .enable("false")) multiplexer_1 (
    .in0(adder_1_out), .in1(subtractor_1_out), .out(out_4), .sel(Add_Sub_control));
  Multiplexer #(.enable("false")) multiplexer_2 (
    .in0(adder_1_cout), .in1(subtractor_1_bout), .out(carry_out), .sel(Add_Sub_control));
endmodule

module ALU (
  input  [3:0] ALUCtl,
  input  [31:0] A,
  input  [31:0] B,
  input  [4:0] Shamt,
  output [31:0] ALUResult,
  output Zero,
  output Overflow
);

  wire comparator_1_lt, comparator_2_lt, comparator_3_eq, comparator_4_eq, or_2_out;
  wire [31:0] Add, And, LessThan, LessThanUnsigned, Nor, Or, ShiftLeft, ShiftRight, Sub, Xor;

  // Probe on ALUCtl
  assign Nor = ~(A | B);  // NOR_Gate nor_1, 32 bits wide
  Adder #(.width(32)) adder_1 (.a(A), .b(B), .out(Add));  // open: cin, cout
  Subtractor #(.width(32)) subtractor_1 (.a(A), .b(B), .out(Sub));  // open: bin, bout
  assign And = A & B;  // AND_Gate and_1, 32 bits wide
  assign Or = A | B;  // OR_Gate or_1, 32 bits wide
  assign Xor = A ^ B;  // XOR_Gate xor_1, 32 bits wide
  Comparator #(.width(32)) comparator_1 (.a(A), .b(B), .lt(comparator_1_lt));  // open: gt, eq
  assign LessThan = {{31{1'b0}}, comparator_1_lt};  // Bit_Extender bit_extender_1
  Shifter #(.width(32)) shifter_1 (.in(B), .\dist (Shamt), .out(ShiftLeft));
  Shifter #(.width(32), .shift("lr")) shifter_2 (.in(B), .\dist (Shamt), .out(ShiftRight));
  Comparator #(.width(32), .mode("unsigned")) comparator_2 (.a(A), .b(B), .lt(comparator_2_lt));  // open: gt, eq
  assign LessThanUnsigned = {{31{1'b0}}, comparator_2_lt};  // Bit_Extender bit_extender_2
  Multiplexer #(.select(4), .width(32), .enable("false")) multiplexer_1 (
    .in0(Or), .in1(LessThanUnsigned), .in2(LessThan), .in3(Add), .in4(Sub), .in5(Xor), .in6(And),
    .in14(ShiftRight), .in15(ShiftLeft), .out(ALUResult), .sel(ALUCtl));  // open: in7, in8, in9, in10, in11, in12, in13
  Comparator #(.width(4)) comparator_3 (.a(4'b0011), .b(ALUCtl), .eq(comparator_3_eq));  // open: gt, lt
  Comparator #(.width(4)) comparator_4 (.a(ALUCtl), .b(4'b0100), .eq(comparator_4_eq));  // open: gt, lt
  Overflow overflow_1 (
    .Add(comparator_3_eq), .Sub(comparator_4_eq), .ASign(A[31]), .BSign(B[31]), .ResultSign(ALUResult[31]),
    .Overflow(Overflow));
  or or_2 (or_2_out, ALUResult[0], ALUResult[1], ALUResult[2], ALUResult[3], ALUResult[4], ALUResult[5], ALUResult[6], ALUResult[7], ALUResult[8], ALUResult[9], ALUResult[10], ALUResult[11], ALUResult[12], ALUResult[13], ALUResult[14], ALUResult[15], ALUResult[16], ALUResult[17], ALUResult[18], ALUResult[19], ALUResult[20], ALUResult[21], ALUResult[22], ALUResult[23], ALUResult[24], ALUResult[25], ALUResult[26], ALUResult[27], ALUResult[28], ALUResult[29], ALUResult[30], ALUResult[31]);
  not not_1 (Zero, or_2_out);

  // Other names for the same wires on the sheet: ASign = A[31]; ResultSign = ALUResult[31]; BSign = B[31]
endmodule

module Register_File (
  input  [4:0] WrAddr,
  input  [31:0] WrData,
  input  WrReg,
  input  [4:0] RdAddr1,
  input  [4:0] RdAddr2,
  input  Clock,
  output [31:0] RdData1,
  output [31:0] RdData2
);

  wire WrReg0, WrReg1, WrReg2, WrReg3, WrReg4, WrReg5, WrReg6, WrReg7, WrReg8, WrReg9, WrReg10, WrReg11,
       WrReg12, WrReg13, WrReg14, WrReg15, WrReg16, WrReg17, WrReg18, WrReg19, WrReg20, WrReg21, WrReg22,
       WrReg23, WrReg24, WrReg25, WrReg26, WrReg27, WrReg28, WrReg29, WrReg30, WrReg31;
  wire [31:0] RegData1, RegData2, RegData3, RegData4, RegData5, RegData6, RegData7, RegData8, RegData9,
       RegData10, RegData11, RegData12, RegData13, RegData14, RegData15, RegData16, RegData17, RegData18,
       RegData19, RegData20, RegData21, RegData22, RegData23, RegData24, RegData25, RegData26, RegData27,
       RegData28, RegData29, RegData30, RegData31;

  Demultiplexer #(.select(5), .enable("false")) demultiplexer_1 (
    .out0(WrReg0), .out1(WrReg1), .out2(WrReg2), .out3(WrReg3), .out4(WrReg4), .out5(WrReg5), .out6(WrReg6),
    .out7(WrReg7), .out8(WrReg8), .out9(WrReg9), .out10(WrReg10), .out11(WrReg11), .out12(WrReg12),
    .out13(WrReg13), .out14(WrReg14), .out15(WrReg15), .out16(WrReg16), .out17(WrReg17), .out18(WrReg18),
    .out19(WrReg19), .out20(WrReg20), .out21(WrReg21), .out22(WrReg22), .out23(WrReg23), .out24(WrReg24),
    .out25(WrReg25), .out26(WrReg26), .out27(WrReg27), .out28(WrReg28), .out29(WrReg29), .out30(WrReg30),
    .out31(WrReg31), .in(WrReg), .sel(WrAddr));
  // Probe on RegData4
  Register #(.width(32)) Reg4 (.D(WrData), .en(WrReg4), .Q(RegData4), .clk(Clock));  // open: clr
  // Probe on RegData8
  Register #(.width(32)) Reg8 (.D(WrData), .en(WrReg8), .Q(RegData8), .clk(Clock));  // open: clr
  // Probe on RegData12
  Register #(.width(32)) Reg12 (.D(WrData), .en(WrReg12), .Q(RegData12), .clk(Clock));  // open: clr
  // Probe on RegData16
  Register #(.width(32)) Reg16 (.D(WrData), .en(WrReg16), .Q(RegData16), .clk(Clock));  // open: clr
  // Probe on RegData20
  Register #(.width(32)) Reg20 (.D(WrData), .en(WrReg20), .Q(RegData20), .clk(Clock));  // open: clr
  // Probe on RegData24
  Register #(.width(32)) Reg24 (.D(WrData), .en(WrReg24), .Q(RegData24), .clk(Clock));  // open: clr
  // Probe on RegData28
  Register #(.width(32)) Reg28 (.D(WrData), .en(WrReg28), .Q(RegData28), .clk(Clock));  // open: clr
  Register #(.width(32)) Reg1 (.D(WrData), .en(WrReg1), .Q(RegData1), .clk(Clock));  // open: clr
  Register #(.width(32)) Reg5 (.D(WrData), .en(WrReg5), .Q(RegData5), .clk(Clock));  // open: clr
  Register #(.width(32)) Reg9 (.D(WrData), .en(WrReg9), .Q(RegData9), .clk(Clock));  // open: clr
  Register #(.width(32)) Reg13 (.D(WrData), .en(WrReg13), .Q(RegData13), .clk(Clock));  // open: clr
  Register #(.width(32)) Reg17 (.D(WrData), .en(WrReg17), .Q(RegData17), .clk(Clock));  // open: clr
  Register #(.width(32)) Reg21 (.D(WrData), .en(WrReg21), .Q(RegData21), .clk(Clock));  // open: clr
  Register #(.width(32)) Reg25 (.D(WrData), .en(WrReg25), .Q(RegData25), .clk(Clock));  // open: clr
  Register #(.width(32)) Reg29 (.D(WrData), .en(WrReg29), .Q(RegData29), .clk(Clock));  // open: clr
  // Probe on RegData1
  // Probe on RegData5
  // Probe on RegData9
  // Probe on RegData13
  // Probe on RegData17
  // Probe on RegData21
  // Probe on RegData25
  // Probe on RegData29
  // Probe on RegData2
  Register #(.width(32)) Reg2 (.D(WrData), .en(WrReg2), .Q(RegData2), .clk(Clock));  // open: clr
  // Probe on RegData6
  Register #(.width(32)) Reg6 (.D(WrData), .en(WrReg6), .Q(RegData6), .clk(Clock));  // open: clr
  // Probe on RegData10
  Register #(.width(32)) Reg10 (.D(WrData), .en(WrReg10), .Q(RegData10), .clk(Clock));  // open: clr
  // Probe on RegData14
  Register #(.width(32)) Reg14 (.D(WrData), .en(WrReg14), .Q(RegData14), .clk(Clock));  // open: clr
  // Probe on RegData18
  Register #(.width(32)) Reg18 (.D(WrData), .en(WrReg18), .Q(RegData18), .clk(Clock));  // open: clr
  // Probe on RegData22
  Register #(.width(32)) Reg22 (.D(WrData), .en(WrReg22), .Q(RegData22), .clk(Clock));  // open: clr
  // Probe on RegData26
  Register #(.width(32)) Reg26 (.D(WrData), .en(WrReg26), .Q(RegData26), .clk(Clock));  // open: clr
  // Probe on RegData30
  Register #(.width(32)) Reg30 (.D(WrData), .en(WrReg30), .Q(RegData30), .clk(Clock));  // open: clr
  // Probe on RegData3
  Register #(.width(32)) Reg3 (.D(WrData), .en(WrReg3), .Q(RegData3), .clk(Clock));  // open: clr
  // Probe on RegData7
  Register #(.width(32)) Reg7 (.D(WrData), .en(WrReg7), .Q(RegData7), .clk(Clock));  // open: clr
  // Probe on RegData11
  Register #(.width(32)) Reg11 (.D(WrData), .en(WrReg11), .Q(RegData11), .clk(Clock));  // open: clr
  // Probe on RegData15
  Register #(.width(32)) Reg15 (.D(WrData), .en(WrReg15), .Q(RegData15), .clk(Clock));  // open: clr
  // Probe on RegData19
  Register #(.width(32)) Reg19 (.D(WrData), .en(WrReg19), .Q(RegData19), .clk(Clock));  // open: clr
  // Probe on RegData23
  Register #(.width(32)) Reg23 (.D(WrData), .en(WrReg23), .Q(RegData23), .clk(Clock));  // open: clr
  // Probe on RegData27
  Register #(.width(32)) Reg27 (.D(WrData), .en(WrReg27), .Q(RegData27), .clk(Clock));  // open: clr
  // Probe on RegData31
  Register #(.width(32)) Reg31 (.D(WrData), .en(WrReg31), .Q(RegData31), .clk(Clock));  // open: clr
  Multiplexer #(.select(5), .width(32), .enable("false")) multiplexer_1 (
    .in0({32{1'b0}}), .in1(RegData1), .in2(RegData2), .in3(RegData3), .in4(RegData4), .in5(RegData5),
    .in6(RegData6), .in7(RegData7), .in8(RegData8), .in9(RegData9), .in10(RegData10), .in11(RegData11),
    .in12(RegData12), .in13(RegData13), .in14(RegData14), .in15(RegData15), .in16(RegData16),
    .in17(RegData17), .in18(RegData18), .in19(RegData19), .in20(RegData20), .in21(RegData21),
    .in22(RegData22), .in23(RegData23), .in24(RegData24), .in25(RegData25), .in26(RegData26),
    .in27(RegData27), .in28(RegData28), .in29(RegData29), .in30(RegData30), .in31(RegData31), .out(RdData1),
    .sel(RdAddr1));
  Multiplexer #(.select(5), .width(32), .enable("false")) multiplexer_2 (
    .in0({32{1'b0}}), .in1(RegData1), .in2(RegData2), .in3(RegData3), .in4(RegData4), .in5(RegData5),
    .in6(RegData6), .in7(RegData7), .in8(RegData8), .in9(RegData9), .in10(RegData10), .in11(RegData11),
    .in12(RegData12), .in13(RegData13), .in14(RegData14), .in15(RegData15), .in16(RegData16),
    .in17(RegData17), .in18(RegData18), .in19(RegData19), .in20(RegData20), .in21(RegData21),
    .in22(RegData22), .in23(RegData23), .in24(RegData24), .in25(RegData25), .in26(RegData26),
    .in27(RegData27), .in28(RegData28), .in29(RegData29), .in30(RegData30), .in31(RegData31), .out(RdData2),
    .sel(RdAddr2));
endmodule

module Overflow (
  input  Add,
  input  Sub,
  input  ASign,
  input  BSign,
  input  ResultSign,
  output Overflow
);

  wire and_1_out, and_2_out, or_1_out, xnor_1_out, xor_1_out, xor_2_out;

  xnor xnor_1 (xnor_1_out, ASign, BSign);
  xor xor_1 (xor_1_out, ASign, BSign);
  and and_1 (and_1_out, xnor_1_out, Add);
  and and_2 (and_2_out, xor_1_out, Sub);
  or or_1 (or_1_out, and_1_out, and_2_out);
  xor xor_2 (xor_2_out, ResultSign, ASign);
  and and_3 (Overflow, or_1_out, xor_2_out);

  // Notes on the sheet:
  //   Overflow occurs when doing addition and sign(A) == sign(B) && sign(result) != sign(A)
  //   Or
  //   Overflow occurs when doing subtraction and sign(A) != sign(B) && sign(result) != sign(A)
endmodule

module ALUCtl (
  input  [5:0] Op,
  input  [1:0] ALUOp,
  input  [5:0] Func,
  output [3:0] ALUCtl,
  output jr
);

  wire comparator_1_eq, comparator_2_eq;
  wire [3:0] aluctli_1_aluctl0, aluctlr_1_aluctl0;

  ALUCtlI aluctli_1 (
    .Op5(Op[5]), .Op4(Op[4]), .Op3(Op[3]), .Op2(Op[2]), .Op1(Op[1]), .Op0(Op[0]),
    .ALUCtl3(aluctli_1_aluctl0[3]), .ALUCtl2(aluctli_1_aluctl0[2]), .ALUCtl1(aluctli_1_aluctl0[1]),
    .ALUCtl0(aluctli_1_aluctl0[0]));
  ALUCtlR aluctlr_1 (
    .Func5(Func[5]), .Func4(Func[4]), .Func3(Func[3]), .Func2(Func[2]), .Func1(Func[1]), .Func0(Func[0]),
    .ALUCtl3(aluctlr_1_aluctl0[3]), .ALUCtl2(aluctlr_1_aluctl0[2]), .ALUCtl1(aluctlr_1_aluctl0[1]),
    .ALUCtl0(aluctlr_1_aluctl0[0]));
  Comparator #(.width(6)) comparator_1 (.a(Func), .b(6'b001000), .eq(comparator_1_eq));  // open: gt, lt
  Comparator #(.width(2)) comparator_2 (.a(ALUOp), .b(2'b10), .eq(comparator_2_eq));  // open: gt, lt
  Multiplexer #(.select(2), .width(4), .enable("false")) multiplexer_1 (
    .in0(aluctli_1_aluctl0), .in1(4'b0100), .in2(aluctlr_1_aluctl0), .out(ALUCtl), .sel(ALUOp));  // open: in3
  and and_1 (jr, comparator_1_eq, comparator_2_eq);
endmodule

module ALUCtlR (
  input  Func5,
  input  Func4,
  input  Func3,
  input  Func2,
  input  Func1,
  input  Func0,
  output ALUCtl3,
  output ALUCtl2,
  output ALUCtl1,
  output ALUCtl0
);

  wire and_2_out, and_3_out, and_4_out, and_5_out, and_6_out, and_7_out, and_8_out, and_9_out, and_10_out,
       not_1_out, not_2_out, not_3_out, not_4_out, not_5_out, not_6_out, not_7_out, not_8_out, not_9_out,
       not_10_out, not_11_out, not_12_out, not_13_out, not_14_out, not_15_out, not_16_out, not_17_out,
       not_18_out, not_19_out, not_20_out, not_21_out;

  not not_1 (not_1_out, Func5);
  not not_2 (not_2_out, Func4);
  not not_3 (not_3_out, Func3);
  not not_4 (not_4_out, Func2);
  not not_5 (not_5_out, Func0);
  not not_6 (not_6_out, Func5);
  not not_7 (not_7_out, Func4);
  not not_8 (not_8_out, Func3);
  not not_9 (not_9_out, Func0);
  not not_10 (not_10_out, Func3);
  not not_11 (not_11_out, Func0);
  not not_12 (not_12_out, Func5);
  not not_13 (not_13_out, Func4);
  not not_14 (not_14_out, Func2);
  not not_15 (not_15_out, Func0);
  not not_16 (not_16_out, Func1);
  not not_17 (not_17_out, Func0);
  not not_18 (not_18_out, Func0);
  not not_19 (not_19_out, Func2);
  not not_20 (not_20_out, Func1);
  not not_21 (not_21_out, Func2);
  and and_1 (ALUCtl3, not_1_out, not_2_out, not_3_out, not_4_out, not_5_out);
  and and_2 (and_2_out, not_6_out, not_7_out, not_8_out, not_9_out);
  and and_3 (and_3_out, not_10_out, Func1);
  and and_4 (and_4_out, Func2, not_11_out);
  and and_5 (and_5_out, not_12_out, not_13_out, not_14_out, not_15_out);
  and and_6 (and_6_out, not_16_out, not_17_out);
  and and_7 (and_7_out, Func3, not_18_out);
  and and_8 (and_8_out, not_19_out, not_20_out);
  and and_9 (and_9_out, not_21_out, Func0);
  and and_10 (and_10_out, Func2, Func1);
  or or_1 (ALUCtl2, and_2_out, and_3_out, and_4_out);
  or or_2 (ALUCtl1, and_5_out, and_6_out, and_7_out);
  or or_3 (ALUCtl0, and_8_out, and_9_out, and_10_out);
endmodule

module ALUCtlI (
  input  Op5,
  input  Op4,
  input  Op3,
  input  Op2,
  input  Op1,
  input  Op0,
  output ALUCtl3,
  output ALUCtl2,
  output ALUCtl1,
  output ALUCtl0
);

  wire and_2_out, and_3_out, and_4_out, not_1_out, not_2_out, not_3_out, not_4_out, not_5_out;

  not not_1 (not_1_out, Op0);
  not not_2 (not_2_out, Op4);
  not not_3 (not_3_out, Op2);
  not not_4 (not_4_out, Op0);
  not not_5 (not_5_out, Op0);
  not not_6 (ALUCtl0, Op2);
  and and_1 (ALUCtl2, Op2, not_1_out);
  and and_2 (and_2_out, not_2_out, not_3_out);
  and and_3 (and_3_out, Op3, not_4_out);
  and and_4 (and_4_out, Op4, not_5_out);
  or or_1 (ALUCtl1, and_2_out, and_3_out, and_4_out);

  assign ALUCtl3 = 1'b0;
endmodule

module Ctl (
  input  [5:0] Op,
  input  [5:0] Func,
  input  Clock,
  output PCWrite,
  output PCWriteCond,
  output IorD,
  output MemRead,
  output MemWrite,
  output IRWrite,
  output MemtoReg,
  output PCSource1,
  output PCSource0,
  output ALUOp1,
  output ALUOp0,
  output ALUSrcB1,
  output ALUSrcB0,
  output ALUSrcA,
  output RegWrite,
  output RegDst,
  output JAL
);

  wire and_1_out, comparator_2_eq, not_1_out, not_2_out;
  wire [1:0] rom_3_data_2;
  wire [3:0] multiplexer_1_out, register_1_q, rom_1_data, rom_2_data, rom_3_data;
  wire [6:6] comparator_1_eq;

  Comparator #(.width(6)) comparator_1 (.a(Func), .b(6'b001000), .eq(comparator_1_eq[6]));  // open: gt, lt
  Multiplexer #(.select(2), .width(4), .enable("false")) multiplexer_1 (
    .in0(rom_3_data), .in1(rom_1_data), .in2(rom_2_data), .out(multiplexer_1_out), .sel(rom_3_data_2));  // open: in3
  ROM #(.addrWidth(7), .dataWidth(4)) rom_1 (.addr({comparator_1_eq[6], Op}), .data(rom_1_data));  // open: sel
  Register #(.width(4)) register_1 (.D(multiplexer_1_out), .Q(register_1_q), .clk(Clock));  // open: en, clr
  not not_1 (not_1_out, register_1_q[2]);
  not not_2 (not_2_out, register_1_q[1]);
  Comparator #(.width(6)) comparator_2 (.a(Op), .b(6'b000011), .eq(comparator_2_eq));  // open: gt, lt
  ROM #(.addrWidth(6), .dataWidth(4)) rom_2 (.addr(Op), .data(rom_2_data));  // open: sel
  ROM #(.addrWidth(4), .dataWidth(6)) rom_3 (.addr(register_1_q), .data({rom_3_data_2, rom_3_data}));  // open: sel
  and and_1 (and_1_out, register_1_q[3], not_1_out, not_2_out, register_1_q[0]);
  Signals1 signals1_1 (
    .s3(register_1_q[3]), .s2(register_1_q[2]), .s1(register_1_q[1]), .s0(register_1_q[0]),
    .PCWrite(PCWrite), .PCWriteCond(PCWriteCond), .IorD(IorD), .MemRead(MemRead), .MemWrite(MemWrite),
    .IRWrite(IRWrite), .MemtoReg(MemtoReg), .PCSource1(PCSource1), .PCSource0(PCSource0));
  Signals0 signals0_1 (
    .s3(register_1_q[3]), .s2(register_1_q[2]), .s1(register_1_q[1]), .s0(register_1_q[0]), .ALUOp1(ALUOp1),
    .ALUOp0(ALUOp0), .ALUSrcB1(ALUSrcB1), .ALUSrcB0(ALUSrcB0), .ALUSrcA(ALUSrcA), .RegWrite(RegWrite),
    .RegDst(RegDst));
  and and_2 (JAL, and_1_out, comparator_2_eq);

  // Other names for the same wires on the sheet: CLK = Clock

  // Notes on the sheet:
  //   contents of rom_1 (hex, n*v repeats v):
  //   6 9 9 9 8 0 0 0 a 0 0 0 a a 21*0 2 7*0 2 20*0 c
  //   contents of rom_2 (hex, n*v repeats v):
  //   35*0 3 7*0 5
  //   contents of rom_3 (hex, n*v repeats v):
  //   1 10 20 4 0 0 7 0 0 0 b
endmodule

module Signals1 (
  input  s3,
  input  s2,
  input  s1,
  input  s0,
  output PCWrite,
  output PCWriteCond,
  output IorD,
  output MemRead,
  output MemWrite,
  output IRWrite,
  output MemtoReg,
  output PCSource1,
  output PCSource0
);

  wire and_2_out, and_3_out, and_4_out, and_6_out, and_7_out, and_8_out, and_9_out, and_13_out, and_14_out,
       not_1_out, not_2_out, not_3_out, not_4_out, not_5_out, not_6_out, not_7_out, not_8_out, not_9_out,
       not_10_out, not_11_out, not_12_out, not_13_out, not_14_out, not_15_out, not_16_out, not_17_out,
       not_18_out, not_19_out, not_20_out, not_21_out, not_22_out, not_23_out, not_24_out, not_25_out,
       not_26_out, not_27_out, not_28_out, not_29_out, not_30_out, not_31_out, not_32_out, not_33_out,
       not_34_out, not_35_out, not_36_out;

  not not_1 (not_1_out, s3);
  not not_2 (not_2_out, s2);
  not not_3 (not_3_out, s1);
  not not_4 (not_4_out, s0);
  not not_5 (not_5_out, s2);
  not not_6 (not_6_out, s1);
  not not_7 (not_7_out, s1);
  not not_8 (not_8_out, s0);
  not not_9 (not_9_out, s2);
  not not_10 (not_10_out, s1);
  not not_11 (not_11_out, s0);
  not not_12 (not_12_out, s3);
  not not_13 (not_13_out, s2);
  not not_14 (not_14_out, s3);
  not not_15 (not_15_out, s1);
  not not_16 (not_16_out, s3);
  not not_17 (not_17_out, s2);
  not not_18 (not_18_out, s1);
  not not_19 (not_19_out, s0);
  not not_20 (not_20_out, s3);
  not not_21 (not_21_out, s2);
  not not_22 (not_22_out, s3);
  not not_23 (not_23_out, s1);
  not not_24 (not_24_out, s3);
  not not_25 (not_25_out, s2);
  not not_26 (not_26_out, s1);
  not not_27 (not_27_out, s0);
  not not_28 (not_28_out, s3);
  not not_29 (not_29_out, s1);
  not not_30 (not_30_out, s0);
  not not_31 (not_31_out, s2);
  not not_32 (not_32_out, s1);
  not not_33 (not_33_out, s1);
  not not_34 (not_34_out, s0);
  not not_35 (not_35_out, s1);
  and and_1 (PCSource0, s3, not_35_out, not_36_out);
  not not_36 (not_36_out, s0);
  and and_2 (and_2_out, not_1_out, not_2_out, not_3_out, not_4_out);
  or or_1 (PCWrite, and_2_out, and_3_out, and_4_out);
  and and_3 (and_3_out, s3, not_5_out, not_6_out, s0);
  and and_4 (and_4_out, s3, s2, not_7_out, not_8_out);
  and and_5 (PCWriteCond, s3, not_9_out, not_10_out, not_11_out);
  and and_6 (and_6_out, not_12_out, not_13_out, s1, s0);
  or or_2 (IorD, and_6_out, and_7_out);
  and and_7 (and_7_out, not_14_out, s2, not_15_out, s0);
  and and_8 (and_8_out, not_16_out, not_17_out, not_18_out, not_19_out);
  or or_3 (MemRead, and_8_out, and_9_out);
  and and_9 (and_9_out, not_20_out, not_21_out, s1, s0);
  and and_10 (MemWrite, not_22_out, s2, not_23_out, s0);
  and and_11 (IRWrite, not_24_out, not_25_out, not_26_out, not_27_out);
  and and_12 (MemtoReg, not_28_out, s2, not_29_out, not_30_out);
  and and_13 (and_13_out, s3, not_31_out, not_32_out, s0);
  or or_4 (PCSource1, and_13_out, and_14_out);
  and and_14 (and_14_out, s3, s2, not_33_out, not_34_out);
endmodule

module Signals0 (
  input  s3,
  input  s2,
  input  s1,
  input  s0,
  output ALUOp1,
  output ALUOp0,
  output ALUSrcB1,
  output ALUSrcB0,
  output ALUSrcA,
  output RegWrite,
  output RegDst
);

  wire and_2_out, and_3_out, and_6_out, and_7_out, and_8_out, and_9_out, and_10_out, not_1_out, not_2_out,
       not_3_out, not_4_out, not_5_out, not_6_out, not_7_out, not_8_out, not_9_out, not_10_out, not_11_out,
       not_12_out, not_13_out, not_14_out, not_15_out, not_16_out, not_17_out, not_18_out, not_19_out,
       not_20_out, not_21_out, not_22_out, not_23_out;

  not not_1 (not_1_out, s3);
  not not_2 (not_2_out, s0);
  not not_3 (not_3_out, s2);
  not not_4 (not_4_out, s1);
  not not_5 (not_5_out, s0);
  not not_6 (not_6_out, s3);
  not not_7 (not_7_out, s2);
  not not_8 (not_8_out, s1);
  not not_9 (not_9_out, s2);
  not not_10 (not_10_out, s0);
  not not_11 (not_11_out, s3);
  not not_12 (not_12_out, s2);
  and and_1 (ALUSrcB0, not_11_out, not_12_out, not_13_out);
  not not_13 (not_13_out, s1);
  not not_14 (not_14_out, s3);
  and and_2 (and_2_out, not_14_out, s1, not_15_out);
  not not_15 (not_15_out, s0);
  and and_3 (and_3_out, s3, not_16_out, not_17_out);
  not not_16 (not_16_out, s2);
  not not_17 (not_17_out, s0);
  not not_18 (not_18_out, s3);
  not not_19 (not_19_out, s1);
  not not_20 (not_20_out, s0);
  not not_21 (not_21_out, s3);
  not not_22 (not_22_out, s2);
  not not_23 (not_23_out, s3);
  and and_4 (ALUOp1, not_1_out, s2, s1, not_2_out);
  and and_5 (ALUOp0, s3, not_3_out, not_4_out, not_5_out);
  and and_6 (and_6_out, not_6_out, not_7_out, not_8_out, s0);
  or or_1 (ALUSrcB1, and_6_out, and_7_out);
  and and_7 (and_7_out, not_9_out, s1, not_10_out);
  or or_2 (ALUSrcA, and_2_out, and_3_out);
  and and_8 (and_8_out, not_18_out, s2, not_19_out, not_20_out);
  or or_3 (RegWrite, and_8_out, and_9_out, and_10_out);
  and and_9 (and_9_out, not_21_out, s2, s1, s0);
  and and_10 (and_10_out, s3, not_22_out, s1, s0);
  and and_11 (RegDst, not_23_out, s2, s1, s0);
endmodule
